# Fritzing sketch VirtualPresenceRover (saved by Fritzing 0.9.3b)

parts:
  S1 = H-Bridge with L298N
  VCC1 = 4 x AAA Battery Mount  # not connected
  M1 = DC Motor
  Raspberry_Pi1 = Raspberry Pi 2
  M2 = DC Motor
  U1 = SWITCH-SPST-2 [package=switch-spst-vertical]  # not connected
  Reg2 = DC-DC CONVERTER [part_number=80633 package=dc-dc_converter]
  VCC2 = 4 x AAA Battery Mount  # not connected
  U2 = SWITCH-SPST-2 [package=switch-spst-vertical]  # not connected
  U3 = TCM8240MD [package=tcm8240md]  # not connected

nets:
  N1: S1.ENA, Raspberry_Pi1.GPIO14
  N2: S1.IN1, Raspberry_Pi1.GPIO15
  N3: S1.IN2, Raspberry_Pi1.GPIO18
  N4: S1.IN3, Raspberry_Pi1.GPIO8
  N5: S1.IN4, Raspberry_Pi1.GPIO7
  N6: S1.ENB, Raspberry_Pi1.GPIO25
  N7: S1.M1-01, M1.pin_2
  N8: S1.M1-02, M1.pin_1
  N9: S1.M2-01, M2.pin_2
  N10: S1.M2-02, M2.pin_1
  N11: Raspberry_Pi1.GND, Reg2.OUT-
  N12: Raspberry_Pi1.5V, Reg2.OUT+

notes:
  RPi Camera Connected through CSI

custom parts:
  H-Bridge with L298N: h-bridge
  DC-DC CONVERTER: WYHP 5A constant current/voltage manufactured by Shenzhen Weiyapuhua Technology Co., Ltd
